// Logisim project MIPSxy.circ as structural Verilog: 7 circuits, main circuit main
module main (
  input  hold,
  input  reset
);

  wire ALU_ADD2_S, ALU_EQ, ALU_LESS, ALU_MFLO, ALU_MULT, ALU_SUB, and_1_out, clock_1_out, clock_2_out,
       comparator_1_eq, DM_RE, DM_WE, PC_S, RF_R1E, RF_R2E, RF_WE;
  wire [1:0] RF_WA_S, RF_WD_S;
  wire [4:0] multiplexer_2_out;
  wire [9:0] alu_1_s_2, pc_1_pc11_2;
  wire [25:0] rom_1_data;
  wire [31:0] alu_1_s, bit_extender_1_out, buffer_1_out, multiplexer_1_out, multiplexer_3_out, pc_1_pc_4,
       ram_1_data, rf_1_r1d, rf_1_r2d;
  wire [31:26] rom_1_data_2;

  PC pc_1 (.ir25_0(rom_1_data), .pc11_2(pc_1_pc11_2), .pc_s(PC_S), .reset(reset), .pc_4(pc_1_pc_4), .hold(hold));
  ROM #(.addrWidth(10), .dataWidth(32)) rom_1 (.addr(pc_1_pc11_2), .data({rom_1_data_2, rom_1_data}));  // open: sel
  CTRL ctrl_1 (
    .ir31_26(rom_1_data_2), .ir5_0(rom_1_data[5:0]), .alu_eq(ALU_EQ), .rf_wa_s(RF_WA_S), .rf_wd_s(RF_WD_S),
    .rf_we(RF_WE), .rf_r1e(RF_R1E), .rf_r2e(RF_R2E), .alu_add2_s(ALU_ADD2_S), .dm_we(DM_WE), .dm_re(DM_RE),
    .pc_s(PC_S), .alu_sub(ALU_SUB), .alu_less(ALU_LESS), .alu_mflo(ALU_MFLO), .alu_mult(ALU_MULT));
  RF rf_1 (
    .r1a(rom_1_data[25:21]), .r2a(rom_1_data[20:16]), .we(RF_WE), .wa(multiplexer_2_out), .r1d(rf_1_r1d),
    .r2d(rf_1_r2d), .r1e(RF_R1E), .r2e(RF_R2E), .wd(multiplexer_1_out));
  Multiplexer #(.select(2), .width(32)) multiplexer_1 (
    .in0(ram_1_data), .in1({alu_1_s[31:12], alu_1_s_2, alu_1_s[1:0]}), .in2(pc_1_pc_4),
    .out(multiplexer_1_out), .sel(RF_WD_S));  // open: in3, en
  Multiplexer #(.select(2), .width(5)) multiplexer_2 (
    .in0(rom_1_data[15:11]), .in1(rom_1_data[20:16]), .in2({5{1'b1}}), .out(multiplexer_2_out), .sel(RF_WA_S));  // open: in3, en
  assign buffer_1_out = {alu_1_s[31:12], alu_1_s_2, alu_1_s[1:0]};  // Buffer buffer_1, 32 bits wide
  assign bit_extender_1_out = {{16{rom_1_data[15]}}, rom_1_data[15:0]};  // Bit_Extender bit_extender_1
  Clock clock_1 (.out(clock_1_out));
  Comparator #(.width(32)) comparator_1 (.a(32'h2008), .b(buffer_1_out), .eq(comparator_1_eq));  // open: gt, lt
  ALU alu_1 (
    .less(ALU_LESS), .mult(ALU_MULT), .sub(ALU_SUB), .a(rf_1_r1d), .b(multiplexer_3_out),
    .s({alu_1_s[31:12], alu_1_s_2, alu_1_s[1:0]}), .eq(ALU_EQ), .mflo(ALU_MFLO));  // open: less_2, mfhi
  Multiplexer #(.width(32)) multiplexer_3 (
    .in0(bit_extender_1_out), .in1(rf_1_r2d), .out(multiplexer_3_out), .sel(ALU_ADD2_S));  // open: en
  TTY #(.rows(4), .cols(16)) tty_1 (.data(rf_1_r2d[6:0]), .clk(clock_1_out), .we(and_1_out));  // open: clr
  and and_1 (and_1_out, comparator_1_eq, DM_WE);
  // Probe on {alu_1_s[31:12], alu_1_s_2, alu_1_s[1:0]}
  Clock clock_2 (.out(clock_2_out));
  RAM #(.addrWidth(10), .dataWidth(32), .bus("separate")) ram_1 (
    .addr(alu_1_s_2), .din(rf_1_r2d), .data(ram_1_data), .str(DM_WE), .sel(alu_1_s[29]), .clk(clock_2_out),
    .ld(DM_RE));  // open: clr

  // Notes on the sheet:
  //   contents of rom_1 (hex, n*v repeats v):
  //   20082008 2009000c ad090000 20090068 ad090000 2129fffd ad090000 21290007 ad090000 ad090000 21290003
  //   ad090000 20090020 ad090000 20090077 ad090000 2009006f ad090000 20090072 ad090000 2009006c ad090000
  //   20090064 ad090000 8000000
endmodule

module ALU (
  input  mult,
  input  less,
  input  mflo,
  input  mfhi,
  input  sub,
  input  [31:0] a,
  input  [31:0] b,
  output [31:0] s,
  output eq,
  output less_2
);

  wire buffer_1_out, clock_1_out;
  wire [2:0] priority_encoder_1_out;
  wire [31:0] adder_1_out, bit_extender_1_out, HI_q, LO_q, multiplexer_1_out, multiplier_1_cout,
       multiplier_1_out, not_1_out;

  Multiplexer #(.width(32)) multiplexer_1 (.in0(b), .in1(not_1_out), .out(multiplexer_1_out), .sel(sub));  // open: en
  assign not_1_out = ~b;  // NOT_Gate not_1, 32 bits wide
  buf buffer_1 (buffer_1_out, sub);
  Adder #(.width(32)) adder_1 (.a(a), .b(multiplexer_1_out), .out(adder_1_out), .cin(sub));  // open: cout
  Multiplier #(.width(32)) multiplier_1 (.a(a), .b(b), .out(multiplier_1_out), .cout(multiplier_1_cout));  // open: cin
  Comparator #(.width(32)) comparator_1 (.a(a), .b(b), .eq(eq), .lt(less_2));  // open: gt
  assign bit_extender_1_out = {{31{1'b0}}, less_2};  // Bit_Extender bit_extender_1
  Priority_Encoder #(.disabled(0)) priority_encoder_1 (
    .in0(1'b1), .in1(buffer_1_out), .in2(mult), .in3(less), .in4(mflo), .in5(mfhi),
    .out(priority_encoder_1_out));  // open: in6, in7, en_in, gs, en_out
  Register #(.width(32)) LO (.D(multiplier_1_out), .en(mult), .Q(LO_q), .clk(clock_1_out));  // open: clr
  Clock clock_1 (.out(clock_1_out));
  Register #(.width(32)) HI (.D(multiplier_1_cout), .en(mult), .Q(HI_q), .clk(clock_1_out));  // open: clr
  Multiplexer #(.select(3), .width(32)) multiplexer_2 (
    .in0(adder_1_out), .in1(adder_1_out), .in2(multiplier_1_out), .in3(bit_extender_1_out), .in4(LO_q),
    .in5(HI_q), .out(s), .sel(priority_encoder_1_out));  // open: in6, in7, en
endmodule

module RF (
  input  [4:0] r1a,
  input  r1e,
  input  [4:0] r2a,
  input  [31:0] wd,
  input  r2e,
  input  we,
  input  [4:0] wa,
  output [31:0] r1d,
  output [31:0] r2d
);

  wire clock_1_out, E0, E1, E2, E3, E4, E5, E6, E7;
  wire [31:0] multiplexer_1_out, multiplexer_3_out, T0, T1, T2, T3, T4, T5, T6, T7;

  Register #(.width(32)) u_t0 (.D(wd), .en(E0), .Q(T0), .clk(clock_1_out));  // open: clr
  Register #(.width(32)) u_t1 (.D(wd), .en(E1), .Q(T1), .clk(clock_1_out));  // open: clr
  Register #(.width(32)) u_t2 (.D(wd), .en(E2), .Q(T2), .clk(clock_1_out));  // open: clr
  Register #(.width(32)) u_t3 (.D(wd), .en(E3), .Q(T3), .clk(clock_1_out));  // open: clr
  Clock clock_1 (.out(clock_1_out));
  Register #(.width(32)) u_t4 (.D(wd), .en(E4), .Q(T4), .clk(clock_1_out));  // open: clr
  Register #(.width(32)) u_t5 (.D(wd), .en(E5), .Q(T5), .clk(clock_1_out));  // open: clr
  Register #(.width(32)) u_t6 (.D(wd), .en(E6), .Q(T6), .clk(clock_1_out));  // open: clr
  Register #(.width(32)) u_t7 (.D(wd), .en(E7), .Q(T7), .clk(clock_1_out));  // open: clr
  Decoder #(.select(3), .disabled(0)) decoder_1 (
    .out0(E0), .out1(E1), .out2(E2), .out3(E3), .out4(E4), .out5(E5), .out6(E6), .out7(E7), .sel(wa[2:0]),
    .en(we));
  Multiplexer #(.width(32)) multiplexer_1 (
    .in0({32{1'b0}}), .in1(T0), .out(multiplexer_1_out), .sel(r1a[3]));  // open: en
  Multiplexer #(.select(3), .width(32)) multiplexer_2 (
    .in0(multiplexer_1_out), .in1(T1), .in2(T2), .in3(T3), .in4(T4), .in5(T5), .in6(T6), .in7(T7), .out(r1d),
    .sel(r1a[2:0]), .en(r1e));
  Multiplexer #(.width(32)) multiplexer_3 (
    .in0({32{1'b0}}), .in1(T0), .out(multiplexer_3_out), .sel(r2a[3]));  // open: en
  Multiplexer #(.select(3), .width(32)) multiplexer_4 (
    .in0(multiplexer_3_out), .in1(T1), .in2(T2), .in3(T3), .in4(T4), .in5(T5), .in6(T6), .in7(T7), .out(r2d),
    .sel(r2a[2:0]), .en(r2e));
endmodule

module PC (
  input  pc_s,
  input  [25:0] ir25_0,
  input  hold,
  input  reset,
  output [31:0] pc_4,
  output [9:0] pc11_2
);

  wire and_1_out, clock_1_out;
  wire [31:0] multiplexer_1_out, pc_q;

  Adder #(.width(32)) adder_1 (.a({pc_q[31:12], pc11_2, pc_q[1:0]}), .b(32'h4), .out(pc_4));  // open: cin, cout
  Multiplexer #(.width(32)) multiplexer_1 (
    .in0(pc_4), .in1({pc_4[31:28], ir25_0, 2'b00}), .out(multiplexer_1_out), .sel(pc_s));  // open: en
  // Probe on {pc_q[31:12], pc11_2, pc_q[1:0]}
  Register #(.width(32)) pc (
    .D(multiplexer_1_out), .Q({pc_q[31:12], pc11_2, pc_q[1:0]}), .clk(and_1_out), .clr(reset));  // open: en
  and and_1 (and_1_out, ~hold, clock_1_out);  // AND_Gate
  Clock clock_1 (.out(clock_1_out));
endmodule

module CTRL (
  input  [5:0] ir31_26,
  input  [5:0] ir5_0,
  input  alu_eq,
  output [1:0] rf_wa_s,
  output [1:0] rf_wd_s,
  output rf_we,
  output rf_r1e,
  output rf_r2e,
  output alu_add2_s,
  output dm_we,
  output dm_re,
  output pc_s,
  output alu_sub,
  output alu_less,
  output alu_mflo,
  output alu_mult
);

  wire and_1_out, and_5_out, and_7_out, and_8_out, and_9_out, comparator_3_eq, comparator_4_eq,
       comparator_5_eq, comparator_6_eq, comparator_7_eq, comparator_8_eq, comparator_9_eq, comparator_10_eq,
       comparator_11_eq, comparator_12_eq, comparator_13_eq, comparator_14_eq, comparator_16_eq,
       comparator_17_eq, comparator_18_eq, comparator_22_eq, comparator_23_eq, not_1_out;

  Comparator #(.width(6)) comparator_1 (.a(ir31_26), .b(6'b100011), .eq(dm_re));  // open: gt, lt
  Comparator #(.width(6)) comparator_2 (.a(ir31_26), .b(6'b101011), .eq(dm_we));  // open: gt, lt
  Comparator #(.width(6)) comparator_3 (.a(ir31_26), .b(6'b001000), .eq(comparator_3_eq));  // open: gt, lt
  Comparator #(.width(6)) comparator_4 (.a(ir31_26), .b({6{1'b0}}), .eq(comparator_4_eq));  // open: gt, lt
  Comparator #(.width(6)) comparator_5 (.a(ir5_0), .b(6'b100000), .eq(comparator_5_eq));  // open: gt, lt
  Comparator #(.width(6)) comparator_6 (.a(ir31_26), .b({6{1'b0}}), .eq(comparator_6_eq));  // open: gt, lt
  Comparator #(.width(6)) comparator_7 (.a(ir5_0), .b(6'b100010), .eq(comparator_7_eq));  // open: gt, lt
  Comparator #(.width(6)) comparator_8 (.a(ir31_26), .b(6'b000100), .eq(comparator_8_eq));  // open: gt, lt
  Comparator #(.width(6)) comparator_9 (.a(ir5_0), .b(6'b011000), .eq(comparator_9_eq));  // open: gt, lt
  Comparator #(.width(6)) comparator_10 (.a(ir31_26), .b({6{1'b0}}), .eq(comparator_10_eq));  // open: gt, lt
  Comparator #(.width(6)) comparator_11 (.a(ir5_0), .b(6'b010010), .eq(comparator_11_eq));  // open: gt, lt
  Comparator #(.width(6)) comparator_12 (.a(ir31_26), .b(6'b000100), .eq(comparator_12_eq));  // open: gt, lt
  not not_1 (not_1_out, comparator_13_eq);
  Comparator #(.width(6)) comparator_13 (.a(ir5_0), .b(6'b011000), .eq(comparator_13_eq));  // open: gt, lt
  Comparator #(.width(6)) comparator_14 (.a(ir31_26), .b(6'b000101), .eq(comparator_14_eq));  // open: gt, lt
  Comparator #(.width(6)) comparator_15 ();  // open: a, b, gt, eq, lt
  Comparator #(.width(6)) comparator_16 (.a(ir31_26), .b({6{1'b0}}), .eq(comparator_16_eq));  // open: gt, lt
  Comparator #(.width(6)) comparator_17 (.a(ir5_0), .b(6'b101010), .eq(comparator_17_eq));  // open: gt, lt
  Comparator #(.width(6)) comparator_18 (.a(ir31_26), .b(6'b000010), .eq(comparator_18_eq));  // open: gt, lt
  Comparator #(.width(6)) comparator_19 ();  // open: a, b, gt, eq, lt
  Comparator #(.width(6)) comparator_20 (.a(ir31_26), .b(6'b000011), .eq(rf_wa_s[1]));  // open: gt, lt
  Comparator #(.width(6)) comparator_21 ();  // open: a, b, gt, eq, lt
  Comparator #(.width(6)) comparator_22 (.a(ir31_26), .b({6{1'b0}}), .eq(comparator_22_eq));  // open: gt, lt
  Comparator #(.width(6)) comparator_23 (.a(ir5_0), .b(6'b001000), .eq(comparator_23_eq));  // open: gt, lt
  and and_1 (and_1_out, comparator_4_eq, comparator_5_eq);
  and and_2 (alu_sub, comparator_6_eq, comparator_7_eq);
  and and_3 (alu_mult, comparator_8_eq, comparator_9_eq);
  and and_4 (alu_mflo, comparator_10_eq, comparator_11_eq);
  and and_5 (and_5_out, comparator_12_eq, not_1_out);
  and and_6 (alu_less, comparator_16_eq, comparator_17_eq);
  and and_7 (and_7_out, comparator_22_eq, comparator_23_eq);
  and and_8 (and_8_out, and_5_out, alu_eq);
  and and_9 (and_9_out, ~alu_eq, comparator_14_eq);  // AND_Gate
  or or_1 (rf_wa_s[0], dm_re, comparator_3_eq);
  or or_2 (rf_wd_s[0], and_1_out, comparator_3_eq, alu_less, alu_sub);
  or or_3 (rf_we, alu_mflo, dm_re, comparator_3_eq, alu_sub, and_1_out, alu_less, rf_wa_s[1]);
  or or_4 (rf_r1e, and_1_out, dm_re, dm_we, comparator_3_eq, and_7_out, alu_sub, and_5_out, comparator_14_eq, alu_less);
  or or_5 (rf_r2e, dm_we, and_1_out, alu_sub, and_5_out, comparator_14_eq, alu_less);
  or or_6 (alu_add2_s, and_1_out, alu_sub, and_5_out, comparator_14_eq, alu_less);
  or or_7 (pc_s, and_8_out, and_9_out, and_7_out, comparator_18_eq, rf_wa_s[1]);

  assign rf_wd_s[1] = rf_wa_s[1];

  // Notes on the sheet:
  //   lw
  //   sw
  //   addi
  //   add
  //   sub
  //   mult
  //   mflo
  //   beq
  //   bne
  //   slt
  //   j
  //   jal
  //   jr
endmodule

module CTRLif (
  input  [5:0] ir5_0,
  input  [5:0] ir31_26,
  output ir0,
  output ir1,
  output ir2,
  output ir3,
  output ir4,
  output ir5,
  output ir26,
  output i2r7,
  output ir28,
  output ir29,
  output ir30,
  output ir31
);


  assign i2r7 = ir31_26[1];
  assign ir0 = ir5_0[0];
  assign ir1 = ir5_0[1];
  assign ir2 = ir5_0[2];
  assign ir3 = ir5_0[3];
  assign ir4 = ir5_0[4];
  assign ir5 = ir5_0[5];
  assign ir26 = ir31_26[0];
  assign ir28 = ir31_26[2];
  assign ir29 = ir31_26[3];
  assign ir30 = ir31_26[4];
  assign ir31 = ir31_26[5];
endmodule

module PANEL1 (
  input  [31:0] ir,
  output branch,
  output lw,
  output sw,
  output addi,
  output add,
  output sub,
  output mult,
  output slt,
  output jump
);

  wire and_7_out, comparator_4_eq, comparator_5_eq, comparator_6_eq, comparator_7_eq, comparator_8_eq,
       comparator_9_eq, comparator_10_eq, comparator_11_eq, comparator_12_eq, comparator_13_eq,
       comparator_14_eq, comparator_16_eq, comparator_17_eq, comparator_18_eq, comparator_20_eq,
       comparator_22_eq, comparator_23_eq, not_1_out;

  Comparator #(.width(6)) comparator_1 (.a(ir[31:26]), .b(6'b100011), .eq(lw));  // open: gt, lt
  Comparator #(.width(6)) comparator_2 (.a(ir[31:26]), .b(6'b101011), .eq(sw));  // open: gt, lt
  Comparator #(.width(6)) comparator_3 (.a(ir[31:26]), .b(6'b001000), .eq(addi));  // open: gt, lt
  Comparator #(.width(6)) comparator_4 (.a(ir[31:26]), .b({6{1'b0}}), .eq(comparator_4_eq));  // open: gt, lt
  Comparator #(.width(6)) comparator_5 (.a(ir[5:0]), .b(6'b100000), .eq(comparator_5_eq));  // open: gt, lt
  Comparator #(.width(6)) comparator_6 (.a(ir[31:26]), .b({6{1'b0}}), .eq(comparator_6_eq));  // open: gt, lt
  Comparator #(.width(6)) comparator_7 (.a(ir[5:0]), .b(6'b100010), .eq(comparator_7_eq));  // open: gt, lt
  Comparator #(.width(6)) comparator_8 (.a(ir[31:26]), .b(6'b000100), .eq(comparator_8_eq));  // open: gt, lt
  Comparator #(.width(6)) comparator_9 (.a(ir[5:0]), .b(6'b011000), .eq(comparator_9_eq));  // open: gt, lt
  Comparator #(.width(6)) comparator_10 (.a(ir[31:26]), .b({6{1'b0}}), .eq(comparator_10_eq));  // open: gt, lt
  Comparator #(.width(6)) comparator_11 (.a(ir[5:0]), .b(6'b010010), .eq(comparator_11_eq));  // open: gt, lt
  Comparator #(.width(6)) comparator_12 (.a(ir[31:26]), .b(6'b000100), .eq(comparator_12_eq));  // open: gt, lt
  Comparator #(.width(6)) comparator_13 (.a(ir[5:0]), .b(6'b011000), .eq(comparator_13_eq));  // open: gt, lt
  Comparator #(.width(6)) comparator_14 (.a(ir[31:26]), .b(6'b000101), .eq(comparator_14_eq));  // open: gt, lt
  Comparator #(.width(6)) comparator_15 ();  // open: a, b, gt, eq, lt
  Comparator #(.width(6)) comparator_16 (.a(ir[31:26]), .b({6{1'b0}}), .eq(comparator_16_eq));  // open: gt, lt
  Comparator #(.width(6)) comparator_17 (.a(ir[5:0]), .b(6'b100110), .eq(comparator_17_eq));  // open: gt, lt
  Comparator #(.width(6)) comparator_18 (.a(ir[31:26]), .b(6'b000010), .eq(comparator_18_eq));  // open: gt, lt
  Comparator #(.width(6)) comparator_19 ();  // open: a, b, gt, eq, lt
  Comparator #(.width(6)) comparator_20 (.a(ir[31:26]), .b(6'b000011), .eq(comparator_20_eq));  // open: gt, lt
  Comparator #(.width(6)) comparator_21 ();  // open: a, b, gt, eq, lt
  Comparator #(.width(6)) comparator_22 (.a(ir[31:26]), .b({6{1'b0}}), .eq(comparator_22_eq));  // open: gt, lt
  Comparator #(.width(6)) comparator_23 (.a(ir[5:0]), .b(6'b001000), .eq(comparator_23_eq));  // open: gt, lt
  and and_1 (add, comparator_4_eq, comparator_5_eq);
  and and_2 (sub, comparator_6_eq, comparator_7_eq);
  and and_3 (mult, comparator_8_eq, comparator_9_eq);
  // AND_Gate and_4 has open pins: in0=comparator_10_eq, in1=comparator_11_eq, out=open
  not not_1 (not_1_out, comparator_13_eq);
  and and_5 (slt, comparator_16_eq, comparator_17_eq);
  // AND_Gate and_6 has open pins: in0=comparator_22_eq, in1=comparator_23_eq, out=open
  and and_7 (and_7_out, comparator_12_eq, not_1_out);
  or or_1 (branch, and_7_out, comparator_14_eq);
  or or_2 (jump, comparator_18_eq, comparator_20_eq);

  // Notes on the sheet:
  //   lw
  //   sw
  //   addi
  //   add
  //   sub
  //   mult
  //   mflo
  //   beq
  //   bne
  //   slt
  //   j
  //   jal
  //   jr
endmodule
